# Fritzing sketch laser-sensor (saved by Fritzing 0.9.6b)
breadboards: 1

parts:
  P1 = S1133 Si Photodiode [package="8mm Ceramic [THT]"]
  D1 = Diode [package=diode-hv]
  D2 = Diode [package=diode-hv]
  P2 = S1133 Si Photodiode [package="8mm Ceramic [THT]"]
  WeMos_D1_Mini1 = WeMos D1 Mini
  LED1 = DUO LED RG [package="5 mm [THT]"]
  J1 = Piezo Speaker
  R1 = Resistor [tolerance=±5% resistance=10k package="1206 [SMD]"]

nets:
  N1: P1.cathode, D1.A
  N2: P1.anode, WeMos_D1_Mini1.D7
  N3: D1.C, D2.C, WeMos_D1_Mini1.A0, R1.Pin_0
  N4: D2.A, P2.cathode
  N5: P2.anode, WeMos_D1_Mini1.D6
  N6: WeMos_D1_Mini1.D1, LED1.green_anode
  N7: WeMos_D1_Mini1.D2, LED1.red_anode
  N8: WeMos_D1_Mini1.D5, J1.pin2
  N9: WeMos_D1_Mini1.G, LED1.common_cathode, J1.pin1, R1.Pin_1
